# Fritzing sketch skellington (saved by Fritzing 1.0.0rc)
breadboards: 1

parts:
  KEYPAD1 = Membrane Matrix Keypad
  Pico_H1 = Raspberry Pi Pico H
  Part1 = Adafruit Analog 2-Axis Joystick [part_number="Adafruit #512"]  # not connected

nets:
  N1: KEYPAD1.1, Pico_H1.GP0
  N2: KEYPAD1.2, Pico_H1.GP1
  N3: KEYPAD1.3, Pico_H1.GP2
  N4: KEYPAD1.4, Pico_H1.GP3
  N5: KEYPAD1.5, Pico_H1.GP4
  N6: KEYPAD1.6, Pico_H1.GP5
  N7: KEYPAD1.7, Pico_H1.GP6

custom parts:
  Membrane Matrix Keypad: Membrane Matrix 3x4 Keypad
  Raspberry Pi Pico H: Raspberry Pi Pico H. Based around the RP2040 microcontroller the Pico H is a low cost microcontroller device bringing Raspberry Pi quality, cost, and easy of use to the microcontroller space.
  Adafruit Analog 2-Axis Joystick: This mini-kit makes it easy to mount a PSP/Xbox-like thumb joystick to your project. The thumbstick is an analog joystick - more accurate and sensitive than just 'directional' joysticks - with a 'press in to select' button. Since it's analog, you'll need two analog reading pins on your microcontroller to determine X and Y. Having an extra digital input will let you read the switch. The pack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
