# Fritzing sketch skellington2 (saved by Fritzing 1.0.1rc)
stripboards: 2

parts:
  Part1 = Thumb Joystick
  J1 = Basic Servo
  S1 = Round Pushbutton
  Part2 = TRRS 3.5mm Jack Breakout
  DFPlayer_Mini1 = DFPlayer MINI [package="DIP (Dual Inline) [THT]"]
  Part3 = LCD1602-I2C
  J2 = Power Jack [package=power_jack_smd]
  J3 = Basic Servo
  J4 = Basic Servo
  KEYPAD1 = Membrane Matrix Keypad
  Mod1 = Raspberry Pi Pico

nets:
  GND: Part1.GND, J1.gnd, S1.leg1, Part2.SLEEVE, DFPlayer_Mini1.GND#6, Part3.GND, J2.GND, J3.gnd, J4.gnd, Mod1.pin_3, Mod1.pin_8, Mod1.pin_13, Mod1.pin_18, Mod1.pin_23, Mod1.pin_28, Mod1.pin_33, Mod1.pin_38, Mod1.pin_42
  N1: Part1.HORZ, Mod1.pin_31
  N2: Part1.VERT, Mod1.pin_32
  N3: Part1.VCC, Mod1.pin_36
  VCC: J1.vcc, Part3.VCC, J2.PWR, J3.vcc, J4.vcc, Mod1.pin_39
  N4: J1.pulse, Mod1.pin_4
  N5: S1.leg0, Mod1.pin_1
  N6: Part2.RING1, DFPlayer_Mini1.SPK2
  N7: Part2.TIP, DFPlayer_Mini1.SPK1
  N8: DFPlayer_Mini1.RX, Mod1.pin_21
  N9: DFPlayer_Mini1.TX, Mod1.pin_22
  N10: DFPlayer_Mini1.BUSY, Mod1.pin_24
  N11: Part3.SDA, Mod1.pin_26
  N12: Part3.SCL, Mod1.pin_27
  N13: J3.pulse, Mod1.pin_5
  N14: J4.pulse, Mod1.pin_2
  N15: KEYPAD1.1, Mod1.pin_6
  N16: KEYPAD1.2, Mod1.pin_7
  N17: KEYPAD1.3, Mod1.pin_9
  N18: KEYPAD1.4, Mod1.pin_10
  N19: KEYPAD1.5, Mod1.pin_11
  N20: KEYPAD1.6, Mod1.pin_12
  N21: KEYPAD1.7, Mod1.pin_14

custom parts:
  DFPlayer MINI: MP3 module by DFRobot.com for playing Music from an SD-Card. Supports WAV and MP3 files.
  LCD1602-I2C: A standard character display, usually with 2x16 characters. Comes in many colors with LCM1602 IIC attached.
  Membrane Matrix Keypad: Membrane Matrix 3x4 Keypad
  Raspberry Pi Pico: Raspberry Pi Pico. Based around the RP2040 microcontroller the Pico is a low cost microcontroller device bringing Raspberry Pi quality, cost, and easy of use to the microcontroller space. Jan 2021, Split part in to two versions: SMD (this one) and tht. This one is single sided and uses the castellation pads to solder the module to the board (no holes, other than for the USB connector!). The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
